# Fritzing sketch FreezerThermometer (saved by Fritzing 0.9.1b)
breadboards: 1

parts:
  U1 = TMP36 [package=to-92-kit]
  RedBoard1 = RedBoard [part_number=DEV-11575]
  Part1 = DeuLigne 1.1 - The Snootlab's LCD shield for Arduino
  J1 = Piezo Speaker

nets:
  VCC: U1.VCC, RedBoard1.aref, RedBoard1.3V3
  N1: U1.VOUT, RedBoard1.A1
  GND: U1.GND, RedBoard1.GND, Part1.GND, J1.pin1
  N2: RedBoard1.D3, J1.pin2
  +5V: RedBoard1.+5V, Part1.+5V
  N3: RedBoard1.A4, Part1.A4(SDA)
  N4: RedBoard1.A5, Part1.A5(CLK)

custom parts:
  RedBoard: At SparkFun we use many Arduinos and we're always looking for the simplest, most stable one. Each board is a bit different and no one board has everything we want, so we decided to make our own version that combines all our favorite features. The RedBoard combines the simplicity of the UNO's Optiboot bootloader (which is used in the Pro series), the stability of the FTDI (which we all missed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
